# Fritzing sketch raspiledmeter (saved by Fritzing 0.7.6b)
breadboards: 1

parts:
  Raspberry_Pi1 = Raspberry Pi (Model B)
  R1 = Resistor [tolerance=±5% resistance=330 package=THT]
  R2 = Resistor [tolerance=±5% resistance=330 package=THT]
  R3 = Resistor [tolerance=±5% resistance=330 package=THT]
  R4 = Resistor [tolerance=±5% resistance=330 package=THT]
  R6 = Resistor [tolerance=±5% resistance=330 package=THT]
  R7 = Resistor [tolerance=±5% resistance=330 package=THT]
  R8 = Resistor [tolerance=±5% resistance=330 package=THT]
  R9 = Resistor [tolerance=±5% resistance=330 package=THT]
  LED1 = LED - 5mm [color="Green (555nm)" package="5 mm [THT]"]
  LED3 = LED - 5mm [color="Green (555nm)" package="5 mm [THT]"]
  LED4 = LED - 5mm [color="Green (555nm)" package="5 mm [THT]"]
  LED5 = LED - 5mm [color="Yellow (585nm)" package="5 mm [THT]"]
  LED6 = LED - 5mm [color="Green (555nm)" package="5 mm [THT]"]
  LED7 = LED - 5mm [color="Yellow (585nm)" package="5 mm [THT]"]
  LED8 = smd LED [color="Red (633nm)" package="1206 [SMD]"]
  LED9 = LED - 5mm [color="Green (555nm)" package="5 mm [THT]"]

nets:
  N1: Raspberry_Pi1.GND, LED1.cathode, LED3.cathode, LED4.cathode, LED5.cathode, LED6.cathode, LED7.cathode, LED8.cathode, LED9.cathode
  N2: Raspberry_Pi1.#4, R6.Pin_0
  N3: Raspberry_Pi1.#17, R1.Pin_0
  N4: Raspberry_Pi1.#18, R8.Pin_0
  N5: Raspberry_Pi1.#21, R3.Pin_0
  N6: Raspberry_Pi1.#22, R9.Pin_0
  N7: Raspberry_Pi1.#23, R2.Pin_0
  N8: Raspberry_Pi1.#24, R7.Pin_0
  N9: Raspberry_Pi1.#25, R4.Pin_0
  N10: R1.Pin_1, LED6.anode
  N11: R2.Pin_1, LED7.anode
  N12: R3.Pin_1, LED4.anode
  N13: R4.Pin_1, LED8.anode
  N14: R6.Pin_1, LED3.anode
  N15: R7.Pin_1, LED5.anode
  N16: R8.Pin_1, LED1.anode
  N17: R9.Pin_1, LED9.anode

custom parts:
  Raspberry Pi (Model B): Raspberry Pi Single-board Computer, Model B
